// Logisim project aiALU.circ as structural Verilog: 15 circuits, main circuit ALU
module ALU (
  input  [7:0] A,
  input  [7:0] B,
  input  S2,
  input  S1,
  input  S0,
  input  Cin,
  output [7:0] Y
);

  wire aialu_1_out_7;

  // Probe on A
  aiALU aialu_1 (.in_2(S2), .in_3(S1), .in_4(S0), .out_8(Y), .in_5(Cin), .in_1(A), .in_6(B), .out_7(aialu_1_out_7));
  LED led_1 (.in(aialu_1_out_7));
  // Probe on Y
  // Probe on B
endmodule

module aiALU (
  input  [7:0] in_1,
  input  in_2,
  input  in_3,
  input  in_4,
  input  in_5,
  input  [7:0] in_6,
  output out_7,
  output [7:0] out_8
);

  wire decoder_8bit_1_out_4, decoder_8bit_1_out_5, decoder_8bit_1_out_6, decoder_8bit_1_out_7,
       decoder_8bit_1_out_8, decoder_8bit_1_out_9, decoder_8bit_1_out_10, decoder_8bit_1_out_11;
  wire [7:0] aiarith_1_out_7, ailogic_1_out_9;

  aiLogic ailogic_1 (
    .in_1(in_1), .in_8(in_6), .out_9(ailogic_1_out_9), .in_2(decoder_8bit_1_out_11),
    .in_3(decoder_8bit_1_out_10), .in_4(decoder_8bit_1_out_9), .in_5(decoder_8bit_1_out_8),
    .in_6(decoder_8bit_1_out_7), .in_7(decoder_8bit_1_out_6));
  // Probe on ailogic_1_out_9
  assign out_8 = ailogic_1_out_9 | aiarith_1_out_7;  // OR_Gate or_1, 8 bits wide
  Decoder_8bit decoder_8bit_1 (
    .out_4(decoder_8bit_1_out_4), .out_5(decoder_8bit_1_out_5), .out_6(decoder_8bit_1_out_6),
    .out_7(decoder_8bit_1_out_7), .out_8(decoder_8bit_1_out_8), .out_9(decoder_8bit_1_out_9),
    .out_10(decoder_8bit_1_out_10), .out_11(decoder_8bit_1_out_11), .I2(in_2), .I1(in_3), .I0(in_4));
  aiArith aiarith_1 (
    .A(in_1), .B(in_6), .in_3(in_5), .in_5(decoder_8bit_1_out_5), .out_7(aiarith_1_out_7), .out_6(out_7),
    .in_4(decoder_8bit_1_out_4));
  // Probe on aiarith_1_out_7

  // Other names for the same wires on the sheet: A[7:0] = in_1; B[7:0] = in_6
endmodule

module aiArith (
  input  [7:0] A,
  input  [7:0] B,
  input  in_3,
  input  in_4,
  input  in_5,
  output out_6,
  output [7:0] out_7
);

  wire not_1_out;
  wire [7:0] and_1_out, and_2_out, bit_extender_1_out, bit_extender_2_out, n8bit_adder_1_out_27,
       n8bit_subtractor_1_out_5, not_2_out;

  not not_1 (not_1_out, in_4);
  _8bit_Adder u_8bit_adder_1 (
    .in_17(B[0]), .in_18(A[0]), .in_16(B[1]), .in_15(A[1]), .in_14(B[2]), .in_13(A[2]), .in_12(B[3]),
    .in_11(A[3]), .in_10(B[4]), .in_9(A[4]), .in_8(B[5]), .in_7(A[5]), .in_6(B[6]), .in_5(A[6]), .in_4(B[7]),
    .in_3(A[7]), .out_19(out_6), .out_20(n8bit_adder_1_out_27[7]), .out_21(n8bit_adder_1_out_27[6]),
    .out_22(n8bit_adder_1_out_27[5]), .out_23(n8bit_adder_1_out_27[4]), .out_24(n8bit_adder_1_out_27[3]),
    .out_25(n8bit_adder_1_out_27[2]), .out_26(n8bit_adder_1_out_27[1]), .out_27(n8bit_adder_1_out_27[0]),
    .in_1(not_1_out), .in_2(in_3));
  assign bit_extender_1_out = {{7{not_1_out}}, not_1_out};  // Bit_Extender bit_extender_1
  assign not_2_out = ~bit_extender_1_out;  // NOT_Gate not_2, 8 bits wide
  assign and_1_out = n8bit_adder_1_out_27 & not_2_out;  // AND_Gate and_1, 8 bits wide
  assign bit_extender_2_out = {{7{in_5}}, in_5};  // Bit_Extender bit_extender_2
  assign out_7 = and_1_out | and_2_out;  // OR_Gate or_1, 8 bits wide
  _8bit_Subtractor u_8bit_subtractor_1 (.in_1(A), .in_2(B), .out_5(n8bit_subtractor_1_out_5), .in_3(in_3), .in_4(in_5));
  assign and_2_out = bit_extender_2_out & n8bit_subtractor_1_out_5;  // AND_Gate and_2, 8 bits wide
endmodule

module aiLogic (
  input  [7:0] in_1,
  input  in_2,
  input  in_3,
  input  in_4,
  input  in_5,
  input  in_6,
  input  in_7,
  input  [7:0] in_8,
  output [7:0] out_9
);

  wire and_1_out;
  wire [7:0] a_b_1_out_4, a_b_2_out_4, a_xor_b_1_out_4, bit_extender_1_out, not_a_1_out_3, not_b_1_out_3;

  and and_1 (and_1_out, 1'b0, in_2);
  assign bit_extender_1_out = {{7{and_1_out}}, and_1_out};  // Bit_Extender bit_extender_1
  Not_B not_b_1 (.in_1(in_8), .in_2(in_3), .out_3(not_b_1_out_3));
  Not_A not_a_1 (.in_1(in_1), .out_3(not_a_1_out_3), .in_2(in_4));
  A_xor_B a_xor_b_1 (.in_1(in_1), .in_2(in_8), .out_4(a_xor_b_1_out_4), .in_3(in_5));
  A_B_2 a_b_1 (.in_1(in_1), .in_2(in_8), .out_4(a_b_1_out_4), .in_3(in_6));
  assign out_9 = bit_extender_1_out | not_b_1_out_3 | not_a_1_out_3 | a_xor_b_1_out_4 | a_b_1_out_4 | a_b_2_out_4;  // OR_Gate or_1, 8 bits wide
  A_B a_b_2 (.in_1(in_1), .in_3(in_8), .out_4(a_b_2_out_4), .in_2(in_7));
endmodule

module HalfAdder (
  input  A,
  input  B,
  output S,
  output C
);

  xor xor_1 (S, A, B);
  and and_1 (C, A, B);
endmodule

module FullAdder (
  input  A,
  input  B,
  input  Cin,
  output Cout,
  output S
);

  wire halfadder_1_c, halfadder_2_c, halfadder_2_s;

  or or_1 (Cout, halfadder_2_c, halfadder_1_c);
  HalfAdder halfadder_1 (.A(halfadder_2_s), .B(Cin), .S(S), .C(halfadder_1_c));
  HalfAdder halfadder_2 (.A(A), .B(B), .S(halfadder_2_s), .C(halfadder_2_c));
endmodule

module _8bit_Adder (
  input  in_1,
  input  in_2,
  input  in_3,
  input  in_4,
  input  in_5,
  input  in_6,
  input  in_7,
  input  in_8,
  input  in_9,
  input  in_10,
  input  in_11,
  input  in_12,
  input  in_13,
  input  in_14,
  input  in_15,
  input  in_16,
  input  in_17,
  input  in_18,
  output out_19,
  output out_20,
  output out_21,
  output out_22,
  output out_23,
  output out_24,
  output out_25,
  output out_26,
  output out_27
);

  wire fulladder_2_cout, fulladder_3_cout, fulladder_4_cout, fulladder_5_cout, fulladder_6_cout,
       fulladder_7_cout, fulladder_8_cout, fulladder_9_cout, fulladder_9_s, or_1_out;

  FullAdder fulladder_1 (.A(in_4), .B(in_3), .Cin(fulladder_2_cout), .S(out_20), .Cout(out_19));
  FullAdder fulladder_2 (.A(in_6), .B(in_5), .Cin(fulladder_3_cout), .S(out_21), .Cout(fulladder_2_cout));
  FullAdder fulladder_3 (.A(in_8), .B(in_7), .Cin(fulladder_4_cout), .S(out_22), .Cout(fulladder_3_cout));
  FullAdder fulladder_4 (.A(in_10), .B(in_9), .Cin(fulladder_5_cout), .S(out_23), .Cout(fulladder_4_cout));
  FullAdder fulladder_5 (.A(in_12), .B(in_11), .Cin(fulladder_6_cout), .S(out_24), .Cout(fulladder_5_cout));
  FullAdder fulladder_6 (.A(in_14), .B(in_13), .Cin(fulladder_7_cout), .S(out_25), .Cout(fulladder_6_cout));
  FullAdder fulladder_7 (.A(in_16), .B(in_15), .Cin(fulladder_8_cout), .S(out_26), .Cout(fulladder_7_cout));
  FullAdder fulladder_8 (.A(in_18), .B(in_17), .Cin(or_1_out), .S(out_27), .Cout(fulladder_8_cout));
  FullAdder fulladder_9 (.A(in_2), .B(in_1), .Cin(1'b0), .S(fulladder_9_s), .Cout(fulladder_9_cout));
  or or_1 (or_1_out, fulladder_9_cout, fulladder_9_s);
endmodule

module _8bit_Subtractor (
  input  [7:0] in_1,
  input  [7:0] in_2,
  input  in_3,
  input  in_4,
  output [7:0] out_5
);

  wire [7:0] not_1_out;

  _8bit_Adder2 u_8bit_adder2_1 (
    .in_2(in_1[7]), .in_3(not_1_out[7]), .in_4(in_1[6]), .in_5(not_1_out[6]), .in_6(in_1[5]),
    .in_7(not_1_out[5]), .in_8(in_1[4]), .in_9(not_1_out[4]), .in_10(in_1[3]), .in_11(not_1_out[3]),
    .in_12(in_1[2]), .in_13(not_1_out[2]), .in_14(in_1[1]), .in_15(not_1_out[1]), .in_16(in_1[0]),
    .in_17(not_1_out[0]), .in_1(in_4), .out_20(out_5[7]), .out_21(out_5[6]), .out_22(out_5[5]),
    .out_23(out_5[4]), .out_24(out_5[3]), .out_25(out_5[2]), .out_26(out_5[1]), .out_27(out_5[0]),
    .in_18(in_3));  // open: out_19
  assign not_1_out = ~in_2;  // NOT_Gate not_1, 8 bits wide
endmodule

module _8bit_Adder2 (
  input  in_1,
  input  in_2,
  input  in_3,
  input  in_4,
  input  in_5,
  input  in_6,
  input  in_7,
  input  in_8,
  input  in_9,
  input  in_10,
  input  in_11,
  input  in_12,
  input  in_13,
  input  in_14,
  input  in_15,
  input  in_16,
  input  in_17,
  input  in_18,
  output out_19,
  output out_20,
  output out_21,
  output out_22,
  output out_23,
  output out_24,
  output out_25,
  output out_26,
  output out_27
);

  wire fulladder_2_cout, fulladder_3_cout, fulladder_4_cout, fulladder_5_cout, fulladder_6_cout,
       fulladder_7_cout, fulladder_8_cout, fulladder_9_cout, fulladder_9_s, or_1_out;

  FullAdder fulladder_1 (.A(in_3), .B(in_2), .Cin(fulladder_2_cout), .S(out_20), .Cout(out_19));
  FullAdder fulladder_2 (.A(in_5), .B(in_4), .Cin(fulladder_3_cout), .S(out_21), .Cout(fulladder_2_cout));
  FullAdder fulladder_3 (.A(in_7), .B(in_6), .Cin(fulladder_4_cout), .S(out_22), .Cout(fulladder_3_cout));
  FullAdder fulladder_4 (.A(in_9), .B(in_8), .Cin(fulladder_5_cout), .S(out_23), .Cout(fulladder_4_cout));
  FullAdder fulladder_5 (.A(in_11), .B(in_10), .Cin(fulladder_6_cout), .S(out_24), .Cout(fulladder_5_cout));
  FullAdder fulladder_6 (.A(in_13), .B(in_12), .Cin(fulladder_7_cout), .S(out_25), .Cout(fulladder_6_cout));
  FullAdder fulladder_7 (.A(in_15), .B(in_14), .Cin(fulladder_8_cout), .S(out_26), .Cout(fulladder_7_cout));
  FullAdder fulladder_8 (.A(in_17), .B(in_16), .Cin(or_1_out), .S(out_27), .Cout(fulladder_8_cout));
  FullAdder fulladder_9 (.A(in_1), .B(1'b0), .Cin(in_18), .S(fulladder_9_s), .Cout(fulladder_9_cout));
  or or_1 (or_1_out, fulladder_9_cout, fulladder_9_s);
endmodule

module Not_A (
  input  [7:0] in_1,
  input  in_2,
  output [7:0] out_3
);

  wire [7:0] bit_extender_1_out, not_1_out;

  assign bit_extender_1_out = {{7{in_2}}, in_2};  // Bit_Extender bit_extender_1
  assign not_1_out = ~in_1;  // NOT_Gate not_1, 8 bits wide
  assign out_3 = bit_extender_1_out & not_1_out;  // AND_Gate and_1, 8 bits wide
endmodule

module Not_B (
  input  [7:0] in_1,
  input  in_2,
  output [7:0] out_3
);

  wire [7:0] bit_extender_1_out, not_1_out;

  assign bit_extender_1_out = {{7{in_2}}, in_2};  // Bit_Extender bit_extender_1
  assign not_1_out = ~in_1;  // NOT_Gate not_1, 8 bits wide
  assign out_3 = bit_extender_1_out & not_1_out;  // AND_Gate and_1, 8 bits wide
endmodule

module A_B (
  input  [7:0] in_1,
  input  in_2,
  input  [7:0] in_3,
  output [7:0] out_4
);

  wire [7:0] bit_extender_1_out;

  assign bit_extender_1_out = {{7{in_2}}, in_2};  // Bit_Extender bit_extender_1
  assign out_4 = in_1 & bit_extender_1_out & in_3;  // AND_Gate and_1, 8 bits wide
endmodule

module A_xor_B (
  input  [7:0] in_1,
  input  [7:0] in_2,
  input  in_3,
  output [7:0] out_4
);

  wire [7:0] bit_extender_1_out, xor_1_out;

  assign bit_extender_1_out = {{7{in_3}}, in_3};  // Bit_Extender bit_extender_1
  assign xor_1_out = in_1 ^ in_2;  // XOR_Gate xor_1, 8 bits wide
  assign out_4 = bit_extender_1_out & xor_1_out;  // AND_Gate and_1, 8 bits wide
endmodule

module A_B_2 (
  input  [7:0] in_1,
  input  [7:0] in_2,
  input  in_3,
  output [7:0] out_4
);

  wire [7:0] bit_extender_1_out, or_1_out;

  assign bit_extender_1_out = {{7{in_3}}, in_3};  // Bit_Extender bit_extender_1
  assign or_1_out = in_1 | in_2;  // OR_Gate or_1, 8 bits wide
  assign out_4 = bit_extender_1_out & or_1_out;  // AND_Gate and_1, 8 bits wide
endmodule

module Decoder_8bit (
  input  I2,
  input  I1,
  input  I0,
  output out_4,
  output out_5,
  output out_6,
  output out_7,
  output out_8,
  output out_9,
  output out_10,
  output out_11
);

  wire not_1_out, not_2_out, not_3_out;

  not not_1 (not_1_out, I2);
  not not_2 (not_2_out, I0);
  not not_3 (not_3_out, I1);
  and and_1 (out_4, not_1_out, not_3_out, not_2_out);
  and and_2 (out_5, not_1_out, not_3_out, I0);
  and and_3 (out_6, not_1_out, I1, not_2_out);
  and and_4 (out_7, not_1_out, I1, I0);
  and and_5 (out_8, I2, not_3_out, not_2_out);
  and and_6 (out_9, I2, not_3_out, I0);
  and and_7 (out_10, I2, I1, not_2_out);
  and and_8 (out_11, I0, I1, I2);
endmodule
